// Logisim project ALU8op.circ as structural Verilog: 2 circuits, main circuit ALU8op
// ALU
module ALU8op (
  input  A7,
  input  in_2,
  input  in_3,
  input  in_4,
  input  in_5,
  input  in_6,
  input  in_7,
  input  A0,
  input  B7,
  input  in_10,
  input  in_11,
  input  in_12,
  input  in_13,
  input  in_14,
  input  in_15,
  input  B0,
  input  F0,
  input  F1,
  input  F2,
  output C,
  output Z__1_when_all_output_is_0,
  output out_22,
  output out_23,
  output out_24,
  output out_25,
  output out_26,
  output out_27,
  output out_28,
  output out_29
);

  wire A_1_2_out, alu1b_2_carry_out, alu1b_3_carry_out, alu1b_4_carry_out, alu1b_5_carry_out,
       alu1b_6_carry_out, alu1b_7_carry_out, alu1b_8_carry_out, and_1_out, and_2_out, and_3_out, not_1_out,
       not_2_out, not_3_out, not_4_out, or_1_out, undriven, undriven_2, undriven_3;

  // XOR_Gate A_1 has open pins: in1=undriven, in3=A_1_2_out, out=open
  and A_1_2 (A_1_2_out, undriven_2, undriven_3);
  // AND_Gate COut has open pins: in0=A_1_2_out, in2=undriven, out=open
  ALU1b alu1b_1 (.Carry(alu1b_2_carry_out), .F0(F0), .F1(F1), .F2(F2), .A(A7), .B(B7), .Carry_OUT(C), .OUT(out_22));
  ALU1b alu1b_2 (
    .Carry(alu1b_3_carry_out), .F0(F0), .F1(F1), .F2(F2), .A(in_2), .B(in_10), .Carry_OUT(alu1b_2_carry_out),
    .OUT(out_23));
  ALU1b alu1b_3 (
    .Carry(alu1b_5_carry_out), .F0(F0), .F1(F1), .F2(F2), .A(in_3), .B(in_11), .Carry_OUT(alu1b_3_carry_out),
    .OUT(out_24));
  ALU1b alu1b_4 (
    .Carry(alu1b_7_carry_out), .F0(F0), .F1(F1), .F2(F2), .A(in_5), .B(in_13), .Carry_OUT(alu1b_4_carry_out),
    .OUT(out_26));
  ALU1b alu1b_5 (
    .Carry(alu1b_4_carry_out), .F0(F0), .F1(F1), .F2(F2), .A(in_4), .B(in_12), .Carry_OUT(alu1b_5_carry_out),
    .OUT(out_25));
  ALU1b alu1b_6 (
    .Carry(alu1b_8_carry_out), .F0(F0), .F1(F1), .F2(F2), .A(in_7), .B(in_15), .Carry_OUT(alu1b_6_carry_out),
    .OUT(out_28));
  ALU1b alu1b_7 (
    .Carry(alu1b_6_carry_out), .F0(F0), .F1(F1), .F2(F2), .A(in_6), .B(in_14), .Carry_OUT(alu1b_7_carry_out),
    .OUT(out_27));
  ALU1b alu1b_8 (
    .Carry(or_1_out), .F0(F0), .F1(F1), .F2(F2), .A(A0), .B(B0), .Carry_OUT(alu1b_8_carry_out), .OUT(out_29));
  or or_1 (or_1_out, and_1_out, and_2_out, and_3_out);
  not not_1 (not_1_out, F1);
  and and_1 (and_1_out, F0, not_1_out, F2);
  not not_2 (not_2_out, F2);
  and and_2 (and_2_out, F1, not_2_out, not_4_out);
  not not_3 (not_3_out, F2);
  and and_3 (and_3_out, F0, not_3_out, F1);
  not not_4 (not_4_out, F0);
  and and_4 (Z__1_when_all_output_is_0, ~out_29, ~out_28, ~out_27, ~out_26, ~out_25, ~out_24, ~out_23, ~out_22);  // AND_Gate

  // Notes on the sheet:
  //   A
  //   COut
  //   ALU
  //   B
endmodule

module ALU1b (
  input  A,
  input  B,
  input  Carry,
  input  F0,
  input  F1,
  input  F2,
  output Carry_OUT,
  output OUT
);

  wire A___B_out, A_B_2_out, A_B_3_out, A_B_out, A_OR_B_2_out, A_OR_B_out, A_out, and_1_out, and_2_out,
       and_3_out, and_4_out, and_5_out, B_1_2_out, B_1_3_out, B_1_out, B_nB_out, B_out, COut_2_out, COut_out,
       decoder_1_out0, decoder_1_out1, decoder_1_out2, decoder_1_out3, decoder_1_out4, decoder_1_out5,
       decoder_1_out6, decoder_1_out7, nB_2_out, nB_out, or_2_out, plus_C_out;

  or or_1 (Carry_OUT, and_1_out, and_2_out);
  and and_1 (and_1_out, decoder_1_out3, COut_out);
  and and_2 (and_2_out, COut_2_out, or_2_out);
  or or_2 (or_2_out, decoder_1_out4, decoder_1_out5);
  and u_A (A_out, A, decoder_1_out0);
  and u_B (B_out, decoder_1_out1, B);
  and nB (nB_out, ~B, decoder_1_out2);  // AND_Gate
  and B_1 (B_1_out, Carry, decoder_1_out3);
  xor B_1_2 (B_1_2_out, B, B_1_out);
  and B_1_3 (B_1_3_out, B_1_2_out, decoder_1_out3);
  and COut (COut_out, B_1_out, B);
  xor plus_C (plus_C_out, Carry, A_B_2_out);
  or or_3 (OUT, A_out, B_out, nB_out, B_1_3_out, A_B_out, A___B_out, A_OR_B_2_out, A_B_3_out);
  and and_3 (and_3_out, Carry, A_B_2_out);
  and A_B (A_B_out, plus_C_out, decoder_1_out4);
  or A_OR_B (A_OR_B_out, A, B);
  xor A_B_2 (A_B_2_out, A, B_nB_out);
  or COut_2 (COut_2_out, and_3_out, and_4_out);
  and A___B (A___B_out, plus_C_out, decoder_1_out5);
  or B_nB (B_nB_out, and_5_out, nB_2_out);
  and and_4 (and_4_out, A, B_nB_out);
  and and_5 (and_5_out, B, decoder_1_out4);
  and nB_2 (nB_2_out, ~B, decoder_1_out5);  // AND_Gate
  and A_OR_B_2 (A_OR_B_2_out, A_OR_B_out, decoder_1_out7);
  and A_B_3 (A_B_3_out, B, A, decoder_1_out6);
  Decoder #(.select(3), .disabled(0), .enable("false")) decoder_1 (
    .out0(decoder_1_out0), .out1(decoder_1_out1), .out2(decoder_1_out2), .out3(decoder_1_out3),
    .out4(decoder_1_out4), .out5(decoder_1_out5), .out6(decoder_1_out6), .out7(decoder_1_out7),
    .sel({F2, F1, F0}));

  // Notes on the sheet:
  //   Out A
  //   Out B
  //   Out A+1
  //   Out B+1
  //   COut
  //   Out A+B A-B
  //   Out AB
  //   A B
endmodule
