// Logisim project Enabler.circ as structural Verilog: 2 circuits, main circuit AND8b
// Enabler
module AND8b (
  input  [7:0] in_1,
  input  Clock,
  output [7:0] out_3
);

  wire [7:0] and_8_out;

  and and_1 (and_8_out[7], in_1[7], Clock);
  and and_2 (and_8_out[6], in_1[6], Clock);
  and and_3 (and_8_out[5], in_1[5], Clock);
  and and_4 (and_8_out[3], in_1[3], Clock);
  and and_5 (and_8_out[4], in_1[4], Clock);
  and and_6 (and_8_out[1], in_1[1], Clock);
  and and_7 (and_8_out[2], in_1[2], Clock);
  assign out_3 = Clock ? and_8_out : 8'bz;  // Controlled_Buffer controlled_buffer_1
  and and_8 (and_8_out[0], in_1[0], Clock);
endmodule

// Enabler
module AND12b (
  input  [11:0] in_1,
  input  En,
  output [11:0] out_3
);

  wire [11:0] and_12_out;

  and and_1 (and_12_out[11], En, in_1[11]);
  and and_2 (and_12_out[9], En, in_1[9]);
  and and_3 (and_12_out[10], En, in_1[10]);
  and and_4 (and_12_out[8], En, in_1[8]);
  and and_5 (and_12_out[7], in_1[7], En);
  and and_6 (and_12_out[6], in_1[6], En);
  and and_7 (and_12_out[5], in_1[5], En);
  and and_8 (and_12_out[3], in_1[3], En);
  and and_9 (and_12_out[4], in_1[4], En);
  and and_10 (and_12_out[1], in_1[1], En);
  and and_11 (and_12_out[2], in_1[2], En);
  assign out_3 = En ? and_12_out : 12'bz;  // Controlled_Buffer controlled_buffer_1
  and and_12 (and_12_out[0], in_1[0], En);
endmodule
