// Logisim project PCadder.circ as structural Verilog: 1 circuit, main circuit PCadder8bit
// PCadder
module PCadder8bit (
  input  Cin,
  input  [7:0] PC,
  input  [7:0] ADD,
  output [7:0] newPC,
  output Cout
);

  wire not_1_out;
  wire [7:0] adder_1_out, adder_2_out;

  Adder adder_1 (.a({8{1'b0}}), .b(PC), .out(adder_1_out), .cin(Cin));  // open: cout
  not not_1 (not_1_out, Cin);
  Adder adder_2 (.a(ADD), .b(PC), .out(adder_2_out), .cout(Cout));  // open: cin
  Multiplexer #(.width(8), .enable("false")) multiplexer_1 (
    .in0(adder_1_out), .in1(adder_2_out), .out(newPC), .sel(not_1_out));
endmodule
