// Logisim project RISC0.8.12.circ as structural Verilog: 1 circuit, main circuit RISC0.8.12
module RISC0_8_12 (
  input  in_1,
  output CarryOut
);

  wire A0, A1, A2, A3, A4, alu8op_1_out_22, alu8op_1_out_23, alu8op_1_out_24, alu8op_1_out_25,
       alu8op_1_out_26, alu8op_1_out_27, alu8op_1_out_28, alu8op_1_out_29,
       alu8op_1_z__1_when_all_output_is_0, and_1_out, and_2_out, and_3_out, and_4_out, and_5_out, B0, B1, B2,
       B3, B4, CK, J, JMZ, ldTOft, LOAD_out, MOV_out, MOV_PC, nand_1_out, nIFU, nor_1_out, not_1_out,
       not_2_out, not_3_out, not_4_out, not_5_out, not_6_out, or_1_out, or_2_out, or_3_out, or_4_out,
       or_5_out, or_6_out, or_7_out, PC, PC_plus_plus_out, write_qn, wrTOft, Z, Za;
  wire [1:0] SH;
  wire [2:0] A, ALU, switch3_1_out, switch3_2_out;
  wire [3:0] OpCode_q;
  wire [5:0] switch6_1_out;
  wire [5:5] decoder_2_out5;
  wire [7:0] and8b_1_out_3, and8b_6_out_3, cutter_1_out, Dest_q, General_q, H, H_q, MAR_q, MDR_q, PC_q,
       pcadder8bit_1_newpc, shifter_1_out_18, switch8_1_out, switch8_2_out, switch8_3_out, switch8_4_out;
  wire [11:0] and12b_1_out_3, bit_extender_1_out, ram_1_data;
  wire [11:8] MBR_q;
  wire [17:0] rom_1_data;

  or or_1 (or_1_out, wrTOft, ~nIFU, ldTOft);  // OR_Gate
  not not_1 (not_1_out, nIFU);
  Register MAR (.D(shifter_1_out_18), .en(switch6_1_out[0]), .Q(MAR_q), .clk(CK), .clr(in_1));
  switch8 switch8_1 (
    .In_0(shifter_1_out_18), .In_1(cutter_1_out), .OUT(switch8_1_out), .En_0(switch6_1_out[1]),
    .En_1(LOAD_out));
  Cutter cutter_1 (.In(ram_1_data), .Out(cutter_1_out));
  and and_1 (and_1_out, switch6_1_out[2], or_2_out);
  or or_2 (or_2_out, MOV_PC, J);
  switch8 switch8_2 (.In_0(H), .In_1(shifter_1_out_18), .OUT(switch8_2_out), .En_0(not_1_out), .En_1(switch6_1_out[4]));
  or or_3 (or_3_out, switch6_1_out[1], LOAD_out);
  and LOAD (LOAD_out, rom_1_data[2], nIFU);
  and and_2 (and_2_out, ~and_1_out, PC);  // AND_Gate
  switch8 switch8_3 (
    .In_0(pcadder8bit_1_newpc), .In_1(shifter_1_out_18), .OUT(switch8_3_out), .En_0(and_2_out),
    .En_1(and_1_out));
  or or_4 (or_4_out, and_2_out, and_1_out);
  AND12b and12b_1 (.in_1(ram_1_data), .En(or_1_out), .out_3(and12b_1_out_3));
  or or_5 (or_5_out, not_1_out, switch6_1_out[4]);
  Register Dest (.D(shifter_1_out_18), .en(switch6_1_out[5]), .Q(Dest_q), .clk(CK), .clr(in_1));
  Register General (.D(shifter_1_out_18), .en(switch6_1_out[3]), .Q(General_q), .clk(CK), .clr(in_1));
  or or_6 (or_6_out, rom_1_data[2], rom_1_data[1]);
  and and_3 (and_3_out, or_6_out, ~or_7_out);  // AND_Gate
  switch8 switch8_4 (.In_0(MAR_q), .In_1(PC_q), .OUT(switch8_4_out), .En_0(and_3_out), .En_1(or_7_out));
  or or_7 (or_7_out, ldTOft, ~nIFU);  // OR_Gate
  Register MDR (.D(switch8_1_out), .en(or_3_out), .Q(MDR_q), .clk(CK), .clr(in_1));
  Register u_PC (.D(switch8_3_out), .en(or_4_out), .Q(PC_q), .clk(CK), .clr(in_1));
  Register #(.width(12), .trigger("high")) MBR (
    .D(and12b_1_out_3), .en(or_1_out), .Q({MBR_q, H}), .clk(CK), .clr(in_1));
  Register #(.trigger("high")) u_H (.D(switch8_2_out), .en(or_5_out), .Q(H_q), .clk(CK), .clr(in_1));
  assign bit_extender_1_out = {{4{1'b0}}, MDR_q};  // Bit_Extender bit_extender_1
  AND8b and8b_1 (.in_1(MDR_q), .Clock(A0), .out_3(and8b_1_out_3));
  AND8b and8b_2 (.in_1(PC_q), .Clock(A1), .out_3(and8b_1_out_3));
  AND8b and8b_3 (.in_1(H_q), .Clock(A3), .out_3(and8b_1_out_3));
  AND8b and8b_4 (.in_1(Dest_q), .Clock(A4), .out_3(and8b_1_out_3));
  AND8b and8b_5 (.in_1(General_q), .Clock(A2), .out_3(and8b_1_out_3));
  not not_2 (not_2_out, and_4_out);
  AND8b and8b_6 (.in_1(MDR_q), .Clock(B0), .out_3(and8b_6_out_3));
  AND8b and8b_7 (.in_1(PC_q), .Clock(B1), .out_3(and8b_6_out_3));
  AND8b and8b_8 (.in_1(H_q), .Clock(B3), .out_3(and8b_6_out_3));
  AND8b and8b_9 (.in_1(Dest_q), .Clock(B4), .out_3(and8b_6_out_3));
  AND8b and8b_10 (.in_1(General_q), .Clock(B2), .out_3(and8b_6_out_3));
  shifter shifter_1 (
    ._7(alu8op_1_out_22), .in_2(alu8op_1_out_23), .in_3(alu8op_1_out_24), .in_4(alu8op_1_out_25),
    .in_5(alu8op_1_out_26), .in_6(alu8op_1_out_27), .in_7(alu8op_1_out_28), ._0(alu8op_1_out_29),
    .out_11(shifter_1_out_18[7]), .out_12(shifter_1_out_18[6]), .out_13(shifter_1_out_18[5]),
    .out_14(shifter_1_out_18[4]), .out_15(shifter_1_out_18[3]), .out_16(shifter_1_out_18[2]),
    .out_17(shifter_1_out_18[1]), .out_18(shifter_1_out_18[0]), .L___R(SH[0]), .Enable(SH[1]));
  RAM #(.dataWidth(12), .bus("separate")) ram_1 (
    .addr(switch8_4_out), .din(bit_extender_1_out), .data(ram_1_data), .str(and_4_out), .sel(1'b1), .clk(CK),
    .ld(not_2_out));  // open: clr
  ALU8op alu8op_1 (
    .A7(and8b_1_out_3[7]), .in_2(and8b_1_out_3[6]), .in_3(and8b_1_out_3[5]), .in_4(and8b_1_out_3[4]),
    .in_5(and8b_1_out_3[3]), .in_6(and8b_1_out_3[2]), .in_7(and8b_1_out_3[1]), .A0(and8b_1_out_3[0]),
    .B7(and8b_6_out_3[7]), .in_10(and8b_6_out_3[6]), .in_11(and8b_6_out_3[5]), .in_12(and8b_6_out_3[4]),
    .in_13(and8b_6_out_3[3]), .in_14(and8b_6_out_3[2]), .in_15(and8b_6_out_3[1]), .B0(and8b_6_out_3[0]),
    .F0(ALU[0]), .F1(ALU[1]), .F2(ALU[2]), .out_22(alu8op_1_out_22), .out_23(alu8op_1_out_23),
    .out_24(alu8op_1_out_24), .out_25(alu8op_1_out_25), .out_26(alu8op_1_out_26), .out_27(alu8op_1_out_27),
    .out_28(alu8op_1_out_28), .out_29(alu8op_1_out_29),
    .Z__1_when_all_output_is_0(alu8op_1_z__1_when_all_output_is_0), .C(CarryOut));
  and and_4 (and_4_out, write_qn, rom_1_data[1]);
  or or_8 (PC, PC_plus_plus_out, nor_1_out);
  nor nor_1 (nor_1_out, PC_plus_plus_out, J);
  nand PC_plus_plus (PC_plus_plus_out, MBR_q[9], MBR_q[10], MBR_q[11]);
  and u_nIFU (nIFU, MBR_q[11], MBR_q[10], ~MBR_q[9]);  // AND_Gate
  and and_5 (and_5_out, MBR_q[11], MBR_q[10], MBR_q[9], MBR_q[8]);
  D_Flip_Flop #(.trigger("high")) write (
    .clk(CK), .D(nIFU), .Q(wrTOft), .Qn(write_qn), .en(rom_1_data[1]));  // open: preset, reset
  PCadder8bit pcadder8bit_1 (.PC(PC_q), .newPC(pcadder8bit_1_newpc), .Cin(PC));  // open: ADD, Cout
  nand nand_1 (nand_1_out, MBR_q[11], MBR_q[10]);
  and MOV (MOV_out, MBR_q[11], ~MBR_q[10], MBR_q[9], MBR_q[8]);  // AND_Gate
  or or_9 (J, and_5_out, JMZ);
  D_Flip_Flop d_ff_1 (
    .clk(CK), .D(alu8op_1_z__1_when_all_output_is_0), .Q(Z), .en(Za), .reset(in_1));  // open: Qn, preset
  not not_3 (not_3_out, nand_1_out);
  switch3 switch3_1 (.In_0(H[6:4]), .In_1(A), .OUT(switch3_1_out), .En_0(MOV_out), .En_1(not_4_out));
  not not_4 (not_4_out, MOV_out);
  Clock clock_1 (.out(CK));
  D_Flip_Flop #(.trigger("high")) load_2 (
    .clk(CK), .D(rom_1_data[2]), .Q(ldTOft), .en(rom_1_data[2]), .reset(not_5_out));  // open: Qn, preset
  not not_5 (not_5_out, CK);
  Register #(.width(4), .trigger("falling")) OpCode (.D(MBR_q), .en(1'b1), .Q(OpCode_q), .clk(CK), .clr(in_1));
  Decoder #(.select(3)) decoder_1 (
    .out0(B0), .out1(B1), .out2(B2), .out3(B3), .out4(B4), .sel(switch3_2_out), .en(1'b1));  // open: out5, out6, out7
  switch3 switch3_2 (.In_0(3'b011), .In_1(H[2:0]), .OUT(switch3_2_out), .En_0(not_3_out), .En_1(nand_1_out));
  Decoder #(.select(3), .disabled(0)) decoder_2 (
    .out0(A0), .out1(A1), .out2(A2), .out3(A3), .out4(A4), .out5(decoder_2_out5[5]), .sel(switch3_1_out));  // open: out6, out7, en
  and and_6 (MOV_PC, ~H[4], H[5], MOV_out);  // AND_Gate
  and and_7 (JMZ, rom_1_data[17], Z);
  ROM #(.addrWidth(4), .dataWidth(19)) rom_1 (
    .addr(OpCode_q), .data({Za, rom_1_data[17], ALU, SH, A, rom_1_data[8:0]}), .sel(1'b1));
  not not_6 (not_6_out, MOV_out);
  switch6 switch6_1 (
    .In_0(rom_1_data[8:3]), .In_1({decoder_2_out5[5], A4, A3, A2, A1, A0}), .OUT(switch6_1_out),
    .En_0(not_6_out), .En_1(MOV_out));

  // Other names for the same wires on the sheet: clr = in_1

  // Notes on the sheet:
  //   rd
  //   LOAD
  //   PC
  //   ft
  //   wr
  //   RAM
  //   STOR
  //   newPC
  //   oldPC
  //   RAM Operations
  //   FETCH manager
  //   Jump carica H in ALU
  //   swB
  //   swA
  //   sempre ON?
  //   sempre ON?
  //   OpDecode
  //   contents of rom_1 (hex, n*v repeats v):
  //   4c100 48100 50900 54900 58900 5c900 40700 44100 47100 45100 0 4000 2 4 30220 10220
  //   sw A/C
endmodule
