// Logisim project Switch.circ as structural Verilog: 5 circuits, main circuit switch2
// sw2
module switch2 (
  input  En_0,
  input  [1:0] In_0,
  input  [1:0] In_1,
  input  En_1,
  output [1:0] OUT
);

  wire [1:0] and_1_out, and_3_out;

  and and_1 (and_1_out[0], In_0[0], En_0);
  and and_2 (and_1_out[1], In_0[1], En_0);
  and and_3 (and_3_out[0], En_1, In_1[0]);
  and and_4 (and_3_out[1], En_1, In_1[1]);
  assign OUT = and_1_out | and_3_out;  // OR_Gate or_1, 2 bits wide
endmodule

// sw3
module switch3 (
  input  En_0,
  input  [2:0] In_0,
  input  [2:0] In_1,
  input  En_1,
  output [2:0] OUT
);

  wire [2:0] and_1_out, and_4_out;

  and and_1 (and_1_out[0], In_0[0], En_0);
  and and_2 (and_1_out[1], In_0[1], En_0);
  and and_3 (and_1_out[2], En_0, In_0[2]);
  and and_4 (and_4_out[0], En_1, In_1[0]);
  and and_5 (and_4_out[1], En_1, In_1[1]);
  and and_6 (and_4_out[2], En_1, In_1[2]);
  assign OUT = and_1_out | and_4_out;  // OR_Gate or_1, 3 bits wide
endmodule

// sw5
module switch5 (
  input  En_0,
  input  [4:0] In_0,
  input  [4:0] In_1,
  input  En_1,
  output [4:0] OUT
);

  wire [4:0] and_1_out, and_6_out;

  and and_1 (and_1_out[0], In_0[0], En_0);
  and and_2 (and_1_out[1], In_0[1], En_0);
  and and_3 (and_1_out[2], In_0[2], En_0);
  and and_4 (and_1_out[3], In_0[3], En_0);
  and and_5 (and_1_out[4], In_0[4], En_0);
  and and_6 (and_6_out[0], En_1, In_1[0]);
  and and_7 (and_6_out[1], En_1, In_1[1]);
  and and_8 (and_6_out[2], En_1, In_1[2]);
  and and_9 (and_6_out[3], En_1, In_1[3]);
  and and_10 (and_6_out[4], En_1, In_1[4]);
  assign OUT = and_1_out | and_6_out;  // OR_Gate or_1, 5 bits wide
endmodule

// sw6
module switch6 (
  input  En_0,
  input  [5:0] In_0,
  input  [5:0] In_1,
  input  En_1,
  output [5:0] OUT
);

  wire [5:0] and_1_out, and_7_out;

  and and_1 (and_1_out[0], En_0, In_0[0]);
  and and_2 (and_1_out[1], In_0[1], En_0);
  and and_3 (and_1_out[2], In_0[2], En_0);
  and and_4 (and_1_out[3], In_0[3], En_0);
  and and_5 (and_1_out[4], In_0[4], En_0);
  and and_6 (and_1_out[5], In_0[5], En_0);
  and and_7 (and_7_out[0], En_1, In_1[0]);
  and and_8 (and_7_out[1], En_1, In_1[1]);
  and and_9 (and_7_out[2], En_1, In_1[2]);
  and and_10 (and_7_out[3], En_1, In_1[3]);
  and and_11 (and_7_out[4], En_1, In_1[4]);
  and and_12 (and_7_out[5], In_1[5], En_1);
  assign OUT = and_1_out | and_7_out;  // OR_Gate or_1, 6 bits wide
endmodule

// sw8
module switch8 (
  input  En_0,
  input  [7:0] In_0,
  input  [7:0] In_1,
  input  En_1,
  output [7:0] OUT
);

  wire [7:0] and_1_out, and_9_out;

  and and_1 (and_1_out[0], En_0, In_0[0]);
  and and_2 (and_1_out[1], In_0[1], En_0);
  and and_3 (and_1_out[2], In_0[2], En_0);
  and and_4 (and_1_out[3], In_0[3], En_0);
  and and_5 (and_1_out[4], In_0[4], En_0);
  and and_6 (and_1_out[5], In_0[5], En_0);
  and and_7 (and_1_out[6], In_0[6], En_0);
  and and_8 (and_1_out[7], In_0[7], En_0);
  and and_9 (and_9_out[0], En_1, In_1[0]);
  and and_10 (and_9_out[1], En_1, In_1[1]);
  and and_11 (and_9_out[2], En_1, In_1[2]);
  and and_12 (and_9_out[3], En_1, In_1[3]);
  and and_13 (and_9_out[4], En_1, In_1[4]);
  and and_14 (and_9_out[5], En_1, In_1[5]);
  and and_15 (and_9_out[6], En_1, In_1[6]);
  and and_16 (and_9_out[7], En_1, In_1[7]);
  assign OUT = and_1_out | and_9_out;  // OR_Gate or_1, 8 bits wide
endmodule
