// Logisim project shifter0L1R+Enable.circ as structural Verilog: 1 circuit, main circuit shifter
// Shifter
module shifter (
  input  _7,
  input  in_2,
  input  in_3,
  input  in_4,
  input  in_5,
  input  in_6,
  input  in_7,
  input  _0,
  input  L___R,
  input  Enable,
  output out_11,
  output out_12,
  output out_13,
  output out_14,
  output out_15,
  output out_16,
  output out_17,
  output out_18
);

  wire and_1_out, and_2_out, and_3_out, and_4_out, and_5_out, and_6_out, and_7_out, and_8_out, and_9_out,
       and_10_out, and_11_out, and_12_out, and_13_out, and_14_out, and_15_out, and_16_out, and_17_out,
       and_18_out, and_19_out, and_20_out, and_21_out, and_22_out, not_1_out;

  and and_1 (and_1_out, _7, ~Enable);  // AND_Gate
  and and_2 (and_2_out, _7, Enable, L___R);
  and and_3 (and_3_out, not_1_out, Enable, in_2);
  and and_4 (and_4_out, in_2, Enable, L___R);
  and and_5 (and_5_out, not_1_out, Enable, in_3);
  and and_6 (and_6_out, in_2, ~Enable);  // AND_Gate
  or or_1 (out_11, and_3_out, and_1_out);
  and and_7 (and_7_out, in_3, Enable, L___R);
  and and_8 (and_8_out, in_3, ~Enable);  // AND_Gate
  or or_2 (out_12, and_2_out, and_6_out, and_5_out);
  and and_9 (and_9_out, not_1_out, Enable, in_4);
  and and_10 (and_10_out, in_4, ~Enable);  // AND_Gate
  or or_3 (out_14, and_7_out, and_10_out, and_11_out);
  or or_4 (out_13, and_4_out, and_8_out, and_9_out);
  and and_11 (and_11_out, not_1_out, Enable, in_5);
  and and_12 (and_12_out, in_4, Enable, L___R);
  or or_5 (out_15, and_12_out, and_15_out, and_14_out);
  and and_13 (and_13_out, in_5, Enable, L___R);
  and and_14 (and_14_out, not_1_out, Enable, in_6);
  and and_15 (and_15_out, in_5, ~Enable);  // AND_Gate
  or or_6 (out_16, and_13_out, and_17_out, and_19_out);
  and and_16 (and_16_out, in_6, Enable, L___R);
  and and_17 (and_17_out, in_6, ~Enable);  // AND_Gate
  or or_7 (out_17, and_16_out, and_20_out, and_21_out);
  and and_18 (and_18_out, in_7, Enable, L___R);
  and and_19 (and_19_out, not_1_out, Enable, in_7);
  and and_20 (and_20_out, in_7, ~Enable);  // AND_Gate
  or or_8 (out_18, and_18_out, and_22_out);
  and and_21 (and_21_out, not_1_out, Enable, _0);
  and and_22 (and_22_out, _0, ~Enable);  // AND_Gate
  not not_1 (not_1_out, L___R);
endmodule
